# Fritzing sketch 4x4 keypad breadboard (saved by Fritzing 0.9.6b)
breadboards: 1

parts:
  J1 = female pin header, 8 pins [form="♀ (female)"]
  R5 = Resistor [tolerance=±5% resistance=220 power=0.25 package=THT]
  R6 = Resistor [tolerance=±5% resistance=1k power=0.25 package=THT]
  Keypad4x1 = Keypad Membran 4x4
  R11 = Resistor [tolerance=±5% resistance=1k power=0.25 package=THT]
  R13 = Resistor [tolerance=±5% resistance=1k power=0.25 package=THT]
  R14 = Resistor [tolerance=±5% resistance=220 power=0.25 package=THT]
  R15 = Resistor [tolerance=±5% resistance=220 power=0.25 package=THT]
  R12 = Resistor [tolerance=±5% power=0.25 resistance=1k package=THT]
  R16 = Resistor [tolerance=±5% resistance=220 power=0.25 package=THT]

nets:
  N1: J1.pin1, Keypad4x1.Pin1
  N2: J1.pin2, Keypad4x1.Pin2
  N3: J1.pin3, Keypad4x1.Pin3
  N4: J1.pin4, Keypad4x1.Pin4
  N5: J1.pin5, R5.Pin_0, Keypad4x1.Pin5, R12.Pin_0
  N6: J1.pin6, Keypad4x1.Pin6, R13.Pin_0, R14.Pin_0
  N7: J1.pin7, Keypad4x1.Pin7, R11.Pin_0, R15.Pin_0
  N8: J1.pin8, R6.Pin_0, Keypad4x1.Pin8, R16.Pin_0
  N9: R6.Pin_1, R11.Pin_1, R13.Pin_1, R12.Pin_1

custom parts:
  Keypad Membran 4x4: Membrane Keypad 4x4 Matrix
